# Fritzing sketch 2018may22 (saved by Fritzing 0.9.2b)
breadboards: 1

parts:
  Part1 = Arduino Uno (Rev3)
  S1 = Pushbutton [package="[THT]"]
  LED1 = LED - 5mm [color="Red (633nm)" package="5 mm [THT]"]
  LED2 = LED - 5mm [color="Red (633nm)" package="5 mm [THT]"]
  R1 = Resistor [tolerance=±5% resistance=1k package=THT]
  R2 = Resistor [tolerance=±5% resistance=1k package=THT]
  R3 = Resistor [tolerance=±5% resistance=10k package=THT]

nets:
  N1: Part1.D12/MISO, R1.Pin_0
  N2: Part1.D13/SCK, R2.Pin_0
  N3: Part1.D2, S1.Pin_1, S1.Pin_2, R3.Pin_1
  N4: Part1.5V, S1.Pin_3, S1.Pin_4
  N5: Part1.GND, LED1.anode, LED2.anode, R3.Pin_0
  N6: LED1.cathode, R1.Pin_1
  N7: LED2.cathode, R2.Pin_1
