# Fritzing sketch 2018may23 (saved by Fritzing 0.9.2b)
breadboards: 1

parts:
  Part1 = Arduino Uno (Rev3)
  S1 = Pushbutton [package="[THT]"]
  LED1 = LED - 5mm [color="Red (633nm)" package="5 mm [THT]"]
  LED2 = LED - 5mm [color="Red (633nm)" package="5 mm [THT]"]
  R1 = Resistor [tolerance=±5% resistance=1k package=THT]
  R2 = Resistor [tolerance=±5% resistance=1k package=THT]
  R3 = Resistor [tolerance=±5% resistance=10k package=THT]
  R4 = Resistor [tolerance=±5% resistance=1k package=THT]
  LED3 = LED - 5mm [color="Red (633nm)" package="5 mm [THT]"]
  R5 = Resistor [tolerance=±5% resistance=5.1k package=THT]
  R6 = Resistor [tolerance=±5% resistance=5.1k package=THT]
  R7 = Resistor [tolerance=±5% resistance=5.1k package=THT]
  U1 = MAGNET [package=magnet-18mm]  # not connected
  U2 = MAGNET [package=magnet-18mm]  # not connected
  U3 = MAGNET [package=magnet-18mm]  # not connected

nets:
  N1: Part1.A0, R5.Pin_1
  N2: Part1.A1, R6.Pin_1
  N3: Part1.A2, R7.Pin_0
  N4: Part1.D11_PWM/MOSI, R4.Pin_1
  N5: Part1.D12/MISO, R1.Pin_1
  N6: Part1.D13/SCK, R2.Pin_1
  N7: Part1.D2, S1.Pin_1, S1.Pin_2, R3.Pin_1
  N8: Part1.5V, S1.Pin_3, S1.Pin_4
  N9: Part1.GND, LED1.cathode, LED2.cathode, R3.Pin_0, LED3.cathode, R5.Pin_0, R6.Pin_0, R7.Pin_1
  N10: LED1.anode, R2.Pin_0
  N11: LED2.anode, R1.Pin_0
  N12: R4.Pin_0, LED3.anode

notes:
  These wires have bare ends to be connected by the magnets
  Magnets (should be strong and light)

custom parts:
  MAGNET: Ceramic disc magnet, COM-08890
